# Fritzing sketch currentSensor (saved by Fritzing 0.9.3b)
breadboards: 1

parts:
  U1 = NodeMCU
  Part1 = Adafruit ADS1115 16Bit I2C ADC [part_number="Adafruit #1085"]
  Part2 = Current Sensor 5A
  U2 = POT [package=trim_pot]

nets:
  N1: U1.connector1, Part1.SCL
  N2: U1.connector2, Part1.SDA
  N3: U1.connector13, Part1.AIN3, Part1.AIN2, Part1.GND, Part2.connector4, U2.A
  N4: U1.connector15, Part1.VDD, Part2.connector2, U2.S
  N5: Part1.AIN1, U2.E
  N6: Part1.AIN0, Part2.connector3

custom parts:
  Adafruit ADS1115 16Bit I2C ADC: For microcontrollers without an analog-to-digital converter or when you want a higher-precision ADC, the ADS1115 provides 16-bit precision at 860 samples/second over I2C. The chip can be configured as 4 single-ended input channels, or two differential channels. As a nice bonus, it even includes a programmable gain amplifier, up to x16, to help boost up smaller single/differential signals to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
